// Logisim project Control.circ as structural Verilog: 1 circuit, main circuit main
module main (
  input  R,
  input  S
);

  wire clock_1_out, not_1_out, or_1_out;

  Clock clock_1 (.out(clock_1_out));
  not not_1 (not_1_out, R);
  or or_1 (or_1_out, not_1_out, S);
  D_Flip_Flop B (.clk(clock_1_out), .D(R), .en(1'b1));  // open: Q, Qn, preset, reset
  D_Flip_Flop A (.clk(clock_1_out), .D(or_1_out), .en(1'b1));  // open: Q, Qn, preset, reset
endmodule
