// Logisim project Display.circ as structural Verilog: 1 circuit, main circuit main
module main (
  input  K,
  input  X,
  input  Y,
  input  Z,
  input  R
);

  wire A_q, A_qn, and_1_out, and_2_out, and_3_out, and_4_out, and_5_out, and_6_out, and_7_out, B_q, B_qn,
       C_q, C_qn, clock_1_out, not_2_out, not_3_out, not_4_out, not_5_out, or_2_out, or_3_out, or_4_out;

  // NOT_Gate not_1 is placed but not wired
  // OR_Gate or_1 is placed but not wired
  Clock clock_1 (.out(clock_1_out));
  D_Flip_Flop C (.clk(clock_1_out), .D(and_2_out), .Q(C_q), .Qn(C_qn), .en(1'b1));  // open: preset, reset
  D_Flip_Flop B (.clk(clock_1_out), .D(or_3_out), .Q(B_q), .Qn(B_qn), .en(1'b1));  // open: preset, reset
  D_Flip_Flop A (.clk(clock_1_out), .D(or_4_out), .Q(A_q), .Qn(A_qn), .en(1'b1));  // open: preset, reset
  and and_1 (and_1_out, Z, K);
  not not_2 (not_2_out, R);
  and and_2 (and_2_out, not_2_out, A_qn, B_q);
  and and_3 (and_3_out, C_qn, B_qn, R, A_q);
  and and_4 (and_4_out, C_qn, B_q, not_3_out, A_qn, Z);
  not not_3 (not_3_out, R);
  and and_5 (and_5_out, C_q, not_4_out);
  not not_4 (not_4_out, R);
  and and_6 (and_6_out, C_qn, B_qn, A_qn);
  and and_7 (and_7_out, C_qn, B_q, A_qn, or_2_out);
  or or_2 (or_2_out, and_1_out, Y);
  or or_3 (or_3_out, and_3_out, and_4_out, and_5_out);
  or or_4 (or_4_out, and_6_out, and_7_out, not_5_out);
  not not_5 (not_5_out, R);
endmodule
